# Fritzing sketch Schematic (saved by Fritzing 0.9.2b)
breadboards: 1

parts:
  Part1 = Arduino Uno (Rev3)
  R1 = Resistor [tolerance=±5% resistance=390 package=THT]
  LED1 = RGB LED - (4 legs) [package="5 mm [THT]"]
  R2 = Resistor [tolerance=±5% resistance=390 package=THT]
  DIN1 = DIN-5 jack (MIDI) [package=THT]
  R3 = Resistor [tolerance=±5% resistance=390 package=THT]

nets:
  N1: Part1.D9_PWM, R2.Pin_0
  N2: Part1.D10_PWM/SS, LED1.green_cathode
  N3: Part1.D11_PWM/MOSI, LED1.blue_cathode
  N4: Part1.D6_PWM, DIN1.5
  N5: Part1.5V, R1.Pin_0, R3.Pin_1
  N6: Part1.GND, DIN1.2
  N7: R1.Pin_1, LED1.common_anode
  N8: LED1.red_cathode, R2.Pin_1
  N9: DIN1.4, R3.Pin_0
